# Fritzing sketch pi_bot (saved by Fritzing 0.9.3b)

parts:
  Raspberry_Pi_Zero1 = Raspberry Pi Zero
  S1 = H-Bridge with L298N
  M3 = fc-51 [package=THT]
  X1 = USB Connectors [package=usb-microb]
  M9 = fc-51 [package=THT]
  M10 = fc-51 [package=THT]
  M11 = fc-51 [package=THT]
  M12 = DC Motor
  M13 = DC Motor
  M14 = DC Motor
  M15 = DC Motor

nets:
  N1: Raspberry_Pi_Zero1.GPIO22, M3.pin1
  N2: Raspberry_Pi_Zero1.GPIO5, M9.pin1
  N3: Raspberry_Pi_Zero1.GPIO6, S1.IN1
  N4: Raspberry_Pi_Zero1.GPIO13, S1.IN2
  N5: Raspberry_Pi_Zero1.GPIO19, S1.IN3
  N6: Raspberry_Pi_Zero1.GPIO26, S1.IN4
  GND: Raspberry_Pi_Zero1.GND, S1.GND, M3.pin2, X1.GND, M9.pin2, M10.pin2, M11.pin2
  N7: Raspberry_Pi_Zero1.GPIO24, M11.pin1
  5V: Raspberry_Pi_Zero1.5V, S1.5V, M3.pin3, X1.VBUS, M9.pin3, M10.pin3, M11.pin3
  N8: S1.M1-01, M12.pin_2, M13.pin_2
  N9: S1.M1-02, M12.pin_1, M13.pin_1
  N10: S1.M2-01, M14.pin_2, M15.pin_2
  N11: S1.M2-02, M14.pin_1, M15.pin_1

custom parts:
  H-Bridge with L298N: h-bridge
